# Fritzing sketch MotorServoController (saved by Fritzing 0.9.3b)
stripboards: 1

parts:
  M1 = RioRand LM2596
  Part2 = Motor Driver 1A Dual TB6612FNG (flipped)
  Part3 = IFR520 MOS module [package=THT]
  J1 = female pin header, 2 pins [form="♀ (female)"]
  WeMos_D1_Mini1 = WeMos D1 Mini
  J2 = female pin header, 2 pins [form="♀ (female)"]
  J3 = female pin header, 2 pins [form="♀ (female)"]
  J4 = female pin header, 2 pins [form="♀ (female)"]
  J6 = female pin header, 2 pins [form="♀ (female)"]
  J7 = female pin header, 2 pins [form="♀ (female)"]
  J8 = female pin header, 2 pins [form="♀ (female)"]

nets:
  N1: M1.Pin_1, J8.pin2
  GND: M1.Pin_2, M1.Pin_4, Part2.GND, Part3.GND, WeMos_D1_Mini1.G, J6.pin1, J7.pin2, J8.pin1
  VIN: M1.Pin_3, Part2.VMOT, Part3.VIN, WeMos_D1_Mini1.5V, J6.pin2
  N2: Part2.STDBY, Part3.SIG, WeMos_D1_Mini1.D8
  N3: Part2.AIN1, WeMos_D1_Mini1.D3
  N4: Part2.AIN2, WeMos_D1_Mini1.D4
  N5: Part2.PWMA, WeMos_D1_Mini1.D5
  VCC: Part2.VCC, Part3.VCC, WeMos_D1_Mini1.3V3, J3.pin1
  N6: Part2.AO1, J4.pin1
  N7: Part2.AO2, J4.pin2
  N8: J1.pin1, WeMos_D1_Mini1.TX
  N9: J1.pin2, WeMos_D1_Mini1.RX
  N10: WeMos_D1_Mini1.D1, J2.pin1
  N11: WeMos_D1_Mini1.D2, J2.pin2
  N12: WeMos_D1_Mini1.D6, J3.pin2

notes:
  N/C
  Gnd
  Vcc
  Servo
  RX
  TX
  Quad
  Quad
  Motor
  Motor
  Gnd (M.fet)
  6v (M.fet)

custom parts:
  Motor Driver 1A Dual TB6612FNG (flipped): The TB6612FNG motor driver can control up to two DC motors at a constant current of 1.2A (3.2A peak). Two input signals (IN1 and IN2) can be used to control the motor in one of four function modes - CW, CCW, short-brake, and stop. The two motor outputs (A and B) can be separately controlled, the speed of each motor is controlled via a PWM input signal with a frequency up to 100kHz. The STBY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
